// Digital circuit GPR_Block.dig as structural Verilog
module GPR_Block (
  input  [7:0] DATA_IN,
  input  [1:0] SEL_W,
  input  LD,
  input  CLR,
  input  CLK,
  output [7:0] R0_OUT,
  output [7:0] R1_OUT,
  output [7:0] R2_OUT,
  output [7:0] R3_OUT
);

  wire and_1_out, and_2_out, and_3_out, and_4_out, not_1_out, not_2_out;

  not not_1 (not_1_out, SEL_W[0]);
  not not_2 (not_2_out, SEL_W[1]);
  and and_1 (and_1_out, not_1_out, not_2_out, LD);
  and and_2 (and_2_out, not_2_out, SEL_W[0], LD);
  and and_3 (and_3_out, SEL_W[1], not_1_out, LD);
  and and_4 (and_4_out, SEL_W[0], SEL_W[1], LD);
  Reg8 reg8_1 (.D(DATA_IN), .LD(and_1_out), .CLK(CLK), .CLR(CLR), .Q(R0_OUT));
  Reg8 reg8_2 (.D(DATA_IN), .LD(and_2_out), .CLK(CLK), .CLR(CLR), .Q(R1_OUT));
  Reg8 reg8_3 (.D(DATA_IN), .LD(and_3_out), .CLK(CLK), .CLR(CLR), .Q(R2_OUT));
  Reg8 reg8_4 (.D(DATA_IN), .LD(and_4_out), .CLK(CLK), .CLR(CLR), .Q(R3_OUT));
endmodule
