// Digital circuit IR_block.dig as structural Verilog
module IR_block (
  input  CLK,
  input  LD,
  input  [7:0] DATA_IN,
  output [7:0] IR_OUT
);

  Reg8 reg8_1 (.D(DATA_IN), .LD(LD), .CLK(CLK), .CLR(1'b0), .Q(IR_OUT));
  // Pins of 1 and 8 bits meet at DATA_IN
endmodule
