// Digital circuit PC_Block.dig as structural Verilog
module PC_Block (
  input  CLK,
  input  [7:0] LOAD_VAL,
  input  RST,
  input  INC,
  input  LD,
  output [7:0] PC_OUT
);

  wire [7:0] _8b_adder_s, multiplexer_1_out, multiplexer_2_out, multiplexer_4_out;

  Reg8 PC_REG (.D(multiplexer_4_out), .LD(1'b1), .CLK(CLK), .CLR(1'b0), .Q(PC_OUT));
  Multiplexer #(.Bits(8)) multiplexer_1 (.sel(INC), .in_0(PC_OUT), .in_1(_8b_adder_s), .out(multiplexer_1_out));
  Multiplexer #(.Bits(8)) multiplexer_2 (.sel(LD), .in_0(multiplexer_1_out), .in_1(LOAD_VAL), .out(multiplexer_2_out));
  Multiplexer #(.Bits(8)) multiplexer_3 (.sel(LD), .in_0(multiplexer_1_out), .in_1(LOAD_VAL), .out(multiplexer_2_out));
  Multiplexer #(.Bits(8)) multiplexer_4 (
    .sel(RST), .in_0(multiplexer_2_out), .in_1({8{1'b0}}), .out(multiplexer_4_out));
  Add #(.Bits(8)) _8b_adder (.a(PC_OUT), .b(8'h1), .c_i(1'b0), .s(_8b_adder_s));  // open: c_o
endmodule
