// Digital circuit Reg8.dig as structural Verilog
module Reg8 (
  input  [7:0] D,
  input  LD,
  input  CLK,
  input  CLR,
  output [7:0] Q
);

  wire multiplexer_1_out, multiplexer_2_out, multiplexer_3_out, multiplexer_4_out, multiplexer_5_out,
       multiplexer_6_out, multiplexer_7_out, multiplexer_8_out, multiplexer_9_out, multiplexer_10_out,
       multiplexer_11_out, multiplexer_12_out, multiplexer_13_out, multiplexer_14_out, multiplexer_15_out,
       multiplexer_16_out;

  Multiplexer multiplexer_1 (.sel(LD), .in_0(Q[7]), .in_1(D[7]), .out(multiplexer_1_out));
  Multiplexer multiplexer_2 (.sel(LD), .in_0(Q[6]), .in_1(D[6]), .out(multiplexer_2_out));
  Multiplexer multiplexer_3 (.sel(LD), .in_0(Q[5]), .in_1(D[5]), .out(multiplexer_3_out));
  Multiplexer multiplexer_4 (.sel(CLR), .in_0(multiplexer_1_out), .in_1(1'b0), .out(multiplexer_4_out));
  Multiplexer multiplexer_5 (.sel(LD), .in_0(Q[4]), .in_1(D[4]), .out(multiplexer_5_out));
  Multiplexer multiplexer_6 (.sel(CLR), .in_0(multiplexer_2_out), .in_1(1'b0), .out(multiplexer_6_out));
  Multiplexer multiplexer_7 (.sel(LD), .in_0(Q[3]), .in_1(D[3]), .out(multiplexer_7_out));
  Multiplexer multiplexer_8 (.sel(CLR), .in_0(multiplexer_3_out), .in_1(1'b0), .out(multiplexer_8_out));
  D_FF D7 (.D(multiplexer_4_out), .C(CLK), .Q(Q[7]));  // open: nQ
  Multiplexer multiplexer_9 (.sel(CLR), .in_0(multiplexer_5_out), .in_1(1'b0), .out(multiplexer_9_out));
  D_FF D6 (.D(multiplexer_6_out), .C(CLK), .Q(Q[6]));  // open: nQ
  Multiplexer multiplexer_10 (.sel(LD), .in_0(Q[2]), .in_1(D[2]), .out(multiplexer_10_out));
  Multiplexer multiplexer_11 (.sel(CLR), .in_0(multiplexer_7_out), .in_1(1'b0), .out(multiplexer_11_out));
  D_FF D5 (.D(multiplexer_8_out), .C(CLK), .Q(Q[5]));  // open: nQ
  Multiplexer multiplexer_12 (.sel(LD), .in_0(Q[1]), .in_1(D[1]), .out(multiplexer_12_out));
  Multiplexer multiplexer_13 (.sel(CLR), .in_0(multiplexer_10_out), .in_1(1'b0), .out(multiplexer_13_out));
  D_FF D4 (.D(multiplexer_9_out), .C(CLK), .Q(Q[4]));  // open: nQ
  Multiplexer multiplexer_14 (.sel(LD), .in_0(Q[0]), .in_1(D[0]), .out(multiplexer_14_out));
  D_FF D3 (.D(multiplexer_11_out), .C(CLK), .Q(Q[3]));  // open: nQ
  Multiplexer multiplexer_15 (.sel(CLR), .in_0(multiplexer_12_out), .in_1(1'b0), .out(multiplexer_15_out));
  D_FF D2 (.D(multiplexer_13_out), .C(CLK), .Q(Q[2]));  // open: nQ
  Multiplexer multiplexer_16 (.sel(CLR), .in_0(multiplexer_14_out), .in_1(1'b0), .out(multiplexer_16_out));
  D_FF D1 (.D(multiplexer_15_out), .C(CLK), .Q(Q[1]));  // open: nQ
  D_FF D0 (.D(multiplexer_16_out), .C(CLK), .Q(Q[0]));  // open: nQ
endmodule
