// Digital circuit Registers_SRAM.dig as structural Verilog
module Registers_SRAM (
  input  [7:0] D,
  input  LD,
  input  CLR,
  input  CLK,
  input  [7:0] DATA,
  input  [1:0] SEL,
  input  LD_2,
  input  CLR_2,
  input  clk_2,
  input  RST,
  input  INC,
  input  LD_3,
  input  [7:0] LOAD_VAL,
  input  CLK_3,
  input  [7:0] DATA_IN,
  input  LD_4,
  input  CLK_4,
  input  [3:0] ADDR,
  input  [7:0] DATA_IN_2,
  input  WE,
  input  CLK_5,
  input  CLK_6,
  input  [3:0] SRAM_ADDR,
  input  SRAM_WE,
  input  [7:0] DATA_IN_3,
  input  [1:0] SEL_W,
  input  LD_5,
  input  CLR_3,
  input  IR_LD,
  input  CLK_7
);

  wire [3:0] ir_block_1_p4, ir_block_1_p4_2, pc_block_1_pc_out, pc_block_1_pc_out_2, sram_block_1_data_out;
  wire [7:0] gpr_block_1_r1_out, gpr_block_2_r0_out, gpr_block_2_r1_out, gpr_block_2_r2_out,
       gpr_block_2_r3_out, ir_block_2_p4, reg8_1_q, sram_block_2_data_out;
  wire [7:4] sram_block_1_data_out_2;

  // IR_block ir_block_1: pin names not known; wires that end beside it: CLK_4, LD_4, DATA_IN, {ir_block_1_p4_2, ir_block_1_p4}
  Reg8 reg8_1 (.D(D), .LD(LD), .CLK(CLK), .CLR(CLR), .Q(reg8_1_q));
  GPR_Block gpr_block_1 (
    .DATA_IN(DATA_IN_3), .SEL_W(SEL_W), .LD(LD_5), .CLR(CLR_3), .CLK(CLK_6), .R1_OUT(gpr_block_1_r1_out));  // open: R0_OUT, R2_OUT, R3_OUT
  Seven_Seg_Hex seven_seg_hex_1 (.d(ir_block_1_p4_2), .dp(1'b0));
  PC_Block pc_block_1 (
    .CLK(CLK_3), .LOAD_VAL(LOAD_VAL), .RST(RST), .INC(INC), .LD(LD_3),
    .PC_OUT({pc_block_1_pc_out_2, pc_block_1_pc_out}));
  SRAM_BLOCK sram_block_1 (
    .ADDR(SRAM_ADDR), .DATA_IN(gpr_block_1_r1_out), .WE(SRAM_WE), .CLK(CLK_6),
    .DATA_OUT({sram_block_1_data_out_2, sram_block_1_data_out}));
  // IR_block ir_block_2: pin names not known; wires that end beside it: CLK_7, IR_LD, {sram_block_1_data_out_2, sram_block_1_data_out}, ir_block_2_p4
  Seven_Seg_Hex seven_seg_hex_2 (.d(reg8_1_q[7:4]), .dp(1'b0));
  Seven_Seg_Hex seven_seg_hex_3 (.d(ir_block_1_p4), .dp(1'b0));
  Seven_Seg_Hex seven_seg_hex_4 (.d(reg8_1_q[3:0]), .dp(1'b0));
  Seven_Seg_Hex seven_seg_hex_5 (.d(pc_block_1_pc_out_2), .dp(1'b0));
  Seven_Seg_Hex seven_seg_hex_6 (.d(ir_block_2_p4[7:4]), .dp(1'b0));
  Seven_Seg_Hex seven_seg_hex_7 (.d(sram_block_1_data_out_2), .dp(1'b0));
  Seven_Seg_Hex seven_seg_hex_8 (.d(pc_block_1_pc_out), .dp(1'b0));
  Seven_Seg_Hex seven_seg_hex_9 (.d(ir_block_2_p4[3:0]), .dp(1'b0));
  Seven_Seg_Hex seven_seg_hex_10 (.d(sram_block_1_data_out), .dp(1'b0));
  SRAM_BLOCK sram_block_2 (.ADDR(ADDR), .DATA_IN(DATA_IN_2), .WE(WE), .CLK(CLK_5), .DATA_OUT(sram_block_2_data_out));
  GPR_Block gpr_block_2 (
    .DATA_IN(DATA), .SEL_W(SEL), .LD(LD_2), .CLR(CLR_2), .CLK(clk_2), .R0_OUT(gpr_block_2_r0_out),
    .R1_OUT(gpr_block_2_r1_out), .R2_OUT(gpr_block_2_r2_out), .R3_OUT(gpr_block_2_r3_out));
  Seven_Seg_Hex seven_seg_hex_11 (.d(sram_block_2_data_out[7:4]), .dp(1'b0));
  Seven_Seg_Hex seven_seg_hex_12 (.d(gpr_block_2_r0_out[7:4]), .dp(1'b0));
  Seven_Seg_Hex seven_seg_hex_13 (.d(gpr_block_2_r1_out[7:4]), .dp(1'b0));
  Seven_Seg_Hex seven_seg_hex_14 (.d(gpr_block_2_r2_out[7:4]), .dp(1'b0));
  Seven_Seg_Hex seven_seg_hex_15 (.d(gpr_block_2_r3_out[7:4]), .dp(1'b0));
  Seven_Seg_Hex seven_seg_hex_16 (.d(gpr_block_2_r0_out[3:0]), .dp(1'b0));
  Seven_Seg_Hex seven_seg_hex_17 (.d(gpr_block_2_r1_out[3:0]), .dp(1'b0));
  Seven_Seg_Hex seven_seg_hex_18 (.d(gpr_block_2_r2_out[3:0]), .dp(1'b0));
  Seven_Seg_Hex seven_seg_hex_19 (.d(gpr_block_2_r3_out[3:0]), .dp(1'b0));
  Seven_Seg_Hex seven_seg_hex_20 (.d(sram_block_2_data_out[3:0]), .dp(1'b0));

  // Notes on the sheet:
  //   DEMO 2  (SRAM -> IR)
  //   TEST FOR IR_BLOCK
  //   TEST FOR REG8
  //   TEST FOR PC_BLOCK
  //   DEMO 1 (GPR REGISTER -> SRAM)
  //   TEST FOR SRAM_BLOCK
  //   TEST FOR GPR_BLOCK
endmodule
