// Digital circuit SRAM_BLOCK.dig as structural Verilog
module SRAM_BLOCK (
  input  [3:0] ADDR,
  input  [7:0] DATA_IN,
  input  WE,
  input  CLK,
  output [7:0] DATA_OUT
);

  RAMDualPort #(.AddrBits(4), .Bits(8)) SRAM (.A(ADDR), .Din(DATA_IN), .str(WE), .C(CLK), .ld(1'b1), .D(DATA_OUT));
endmodule
